// Logisim project nonexist.circ as structural Verilog: 2 circuits, main circuit main
module main (
  input  [7:0] In1,
  input  [7:0] In2,
  input  [7:0] in_3,
  input  [7:0] in_4,
  input  [7:0] in_5,
  output [7:0] out_6
);

  wire comp_1_out_7, comp_2_out_7, comp_3_out_7, comp_4_out_7, comp_5_out_7, comp_6_out_7;
  wire [7:0] multiplexer_1_out, multiplexer_2_out, multiplexer_3_out, multiplexer_4_out, multiplexer_5_out;

  comp comp_1 (.In1(In1), .In2(In2), .in_3(in_3), .in_4(in_4), .in_5(in_5), .in_6(8'h6), .out_7(comp_1_out_7));
  Multiplexer #(.width(8)) multiplexer_1 (.in0(8'h6), .out(multiplexer_1_out), .sel(comp_1_out_7));  // open: in1, en
  comp comp_2 (.In1(In1), .In2(In2), .in_3(in_3), .in_4(in_4), .in_5(in_5), .in_6(8'h5), .out_7(comp_2_out_7));
  Multiplexer #(.width(8)) multiplexer_2 (
    .in0(8'h5), .in1(multiplexer_1_out), .out(multiplexer_2_out), .sel(comp_2_out_7));  // open: en
  comp comp_3 (.In1(In1), .In2(In2), .in_3(in_3), .in_4(in_4), .in_5(in_5), .in_6(8'h4), .out_7(comp_3_out_7));
  Multiplexer #(.width(8)) multiplexer_3 (
    .in0(8'h4), .in1(multiplexer_2_out), .out(multiplexer_3_out), .sel(comp_3_out_7));  // open: en
  comp comp_4 (.In1(In1), .In2(In2), .in_3(in_3), .in_4(in_4), .in_5(in_5), .in_6(8'h3), .out_7(comp_4_out_7));
  Multiplexer #(.width(8)) multiplexer_4 (
    .in0(8'h3), .in1(multiplexer_3_out), .out(multiplexer_4_out), .sel(comp_4_out_7));  // open: en
  comp comp_5 (.In1(In1), .In2(In2), .in_3(in_3), .in_4(in_4), .in_5(in_5), .in_6(8'h2), .out_7(comp_5_out_7));
  Multiplexer #(.width(8)) multiplexer_5 (
    .in0(8'h2), .in1(multiplexer_4_out), .out(multiplexer_5_out), .sel(comp_5_out_7));  // open: en
  comp comp_6 (.In1(In1), .In2(In2), .in_3(in_3), .in_4(in_4), .in_5(in_5), .in_6(8'h1), .out_7(comp_6_out_7));
  Multiplexer #(.width(8)) multiplexer_6 (
    .in0(8'h1), .in1(multiplexer_5_out), .out(out_6), .sel(comp_6_out_7));  // open: en

  // Other names for the same wires on the sheet: in3[7:0] = in_3; in4[7:0] = in_4; in5[7:0] = in_5; out[7:0] = out_6
endmodule

module comp (
  input  [7:0] In1,
  input  [7:0] In2,
  input  [7:0] in_3,
  input  [7:0] in_4,
  input  [7:0] in_5,
  input  [7:0] in_6,
  output out_7
);

  wire comparator_1_eq, comparator_2_eq, comparator_3_eq, comparator_4_eq, comparator_5_eq;

  Comparator #(.mode("unsigned")) comparator_1 (.a(in_6), .b(In1), .eq(comparator_1_eq));  // open: gt, lt
  Comparator #(.mode("unsigned")) comparator_2 (.a(in_6), .b(In2), .eq(comparator_2_eq));  // open: gt, lt
  Comparator #(.mode("unsigned")) comparator_3 (.a(in_6), .b(in_3), .eq(comparator_3_eq));  // open: gt, lt
  Comparator #(.mode("unsigned")) comparator_4 (.a(in_6), .b(in_4), .eq(comparator_4_eq));  // open: gt, lt
  Comparator #(.mode("unsigned")) comparator_5 (.a(in_6), .b(in_5), .eq(comparator_5_eq));  // open: gt, lt
  or or_1 (out_7, comparator_1_eq, comparator_2_eq, comparator_3_eq, comparator_4_eq, comparator_5_eq);

  // Other names for the same wires on the sheet: in3[7:0] = in_3; in4[7:0] = in_4; in5[7:0] = in_5; out = out_7;
  //   tmp[7:0] = in_6
endmodule
