// Logisim project walker.circ as structural Verilog: 3 circuits, main circuit main
module main (
  input  [1:0] in_1,
  input  in_2,
  input  in_3,
  output [3:0] out_4
);

  wire [2:0] nextstate_1_out_3, now;
  wire [3:0] bit_extender_1_out;

  nextstate nextstate_1 (.\input (in_1), .now(now), .out_3(nextstate_1_out_3));
  assign bit_extender_1_out = {{1{1'b0}}, nextstate_1_out_3};  // Bit_Extender bit_extender_1
  Adder #(.width(4)) adder_1 (.a(bit_extender_1_out), .b(4'b0001), .out(out_4));  // open: cin, cout
  Register #(.width(3)) register_1 (.D(nextstate_1_out_3), .Q(now), .clk(in_3), .clr(in_2));  // open: en

  // Other names for the same wires on the sheet: clk = in_3; input[1:0] = in_1; output[3:0] = out_4; reset = in_2
endmodule

module nextstate (
  input  [1:0] \input ,
  input  [2:0] now,
  output [2:0] out_3
);

  help help_1 (
    .in1(\input [1]), .in0(\input [0]), .now2(now[2]), .now1(now[1]), .now0(now[0]), .out2(out_3[2]),
    .out1(out_3[1]), .out0(out_3[0]));
endmodule

module help (
  input  in1,
  input  in0,
  input  now2,
  input  now1,
  input  now0,
  output out2,
  output out1,
  output out0
);

  wire and_1_out, and_2_out, and_3_out, and_4_out, and_5_out, and_6_out, and_7_out, and_8_out, and_9_out,
       and_10_out, and_11_out, and_12_out, and_13_out, and_14_out, and_15_out, and_16_out, and_17_out,
       and_18_out, and_19_out, and_20_out, not_1_out, not_2_out, not_3_out, not_4_out, not_5_out, not_6_out,
       not_7_out, not_8_out, not_9_out, not_10_out, not_11_out, not_12_out, not_13_out, not_14_out,
       not_15_out, not_16_out, not_17_out, not_18_out, not_19_out, not_20_out, not_21_out, not_22_out,
       not_23_out, not_24_out, not_25_out, not_26_out, not_27_out, not_28_out, not_29_out, not_30_out,
       not_31_out, not_32_out, not_33_out, not_34_out, not_35_out, not_36_out;

  not not_1 (not_1_out, in1);
  not not_2 (not_2_out, now1);
  not not_3 (not_3_out, now0);
  not not_4 (not_4_out, in0);
  not not_5 (not_5_out, now1);
  not not_6 (not_6_out, now0);
  not not_7 (not_7_out, in0);
  not not_8 (not_8_out, in1);
  not not_9 (not_9_out, in1);
  not not_10 (not_10_out, in0);
  not not_11 (not_11_out, in0);
  not not_12 (not_12_out, in1);
  not not_13 (not_13_out, now2);
  not not_14 (not_14_out, now2);
  not not_15 (not_15_out, in0);
  not not_16 (not_16_out, now2);
  not not_17 (not_17_out, now0);
  not not_18 (not_18_out, now0);
  not not_19 (not_19_out, in0);
  not not_20 (not_20_out, now2);
  not not_21 (not_21_out, now0);
  not not_22 (not_22_out, in1);
  not not_23 (not_23_out, in1);
  not not_24 (not_24_out, in0);
  not not_25 (not_25_out, now1);
  not not_26 (not_26_out, now0);
  not not_27 (not_27_out, in1);
  not not_28 (not_28_out, now2);
  not not_29 (not_29_out, now1);
  not not_30 (not_30_out, now0);
  not not_31 (not_31_out, now0);
  not not_32 (not_32_out, in0);
  not not_33 (not_33_out, now2);
  not not_34 (not_34_out, now0);
  not not_35 (not_35_out, now1);
  not not_36 (not_36_out, now0);
  and and_1 (and_1_out, not_1_out, now2);
  and and_2 (and_2_out, now2, not_2_out, now0);
  and and_3 (and_3_out, now2, now1, not_3_out);
  and and_4 (and_4_out, in1, not_4_out, not_5_out, not_6_out);
  and and_5 (and_5_out, in1, not_7_out, now1, now0);
  and and_6 (and_6_out, not_8_out, now1, now0);
  and and_7 (and_7_out, not_9_out, not_10_out, now2, now0);
  and and_8 (and_8_out, not_11_out, now2, now1);
  and and_9 (and_9_out, not_12_out, in0, not_13_out, now0);
  and and_10 (and_10_out, in0, not_14_out, now1);
  and and_11 (and_11_out, in1, not_15_out, not_16_out, not_17_out);
  and and_12 (and_12_out, in1, in0, now2, not_18_out);
  and and_13 (and_13_out, not_19_out, not_20_out, now1, not_21_out);
  and and_14 (and_14_out, not_22_out, now1, now0);
  and and_15 (and_15_out, not_23_out, not_24_out, now2, not_25_out, not_26_out);
  and and_16 (and_16_out, not_27_out, in0, not_28_out, not_29_out, not_30_out);
  and and_17 (and_17_out, in0, now2, now1, not_31_out);
  and and_18 (and_18_out, in1, not_32_out, not_33_out, not_34_out);
  and and_19 (and_19_out, in1, not_35_out, now0);
  and and_20 (and_20_out, in1, in0, now2, not_36_out);
  or or_1 (out2, and_1_out, and_2_out, and_3_out, and_4_out, and_5_out);
  or or_2 (out1, and_6_out, and_7_out, and_8_out, and_9_out, and_10_out, and_11_out, and_12_out);
  or or_3 (out0, and_13_out, and_14_out, and_15_out, and_16_out, and_17_out, and_18_out, and_19_out, and_20_out);
endmodule
