// Logisim project single_cycle.circ as structural Verilog: 7 circuits, main circuit main
module main (
  input  in_1,
  output [31:0] out_2,
  output [31:0] out_3,
  output out_4,
  output [4:0] out_5,
  output [31:0] out_6,
  output out_7,
  output [31:0] out_8,
  output [31:0] out_9
);

  wire alu_1_equal, and_1_out, and_2_out, clk, control_unit_alusrc1, control_unit_alusrc2,
       control_unit_ext_way, control_unit_reg_dst, inid_1_add, inid_1_beq, inid_1_lui, inid_1_lw, inid_1_ori,
       inid_1_sll, inid_1_sub, inid_1_sw, memToReg, regW_src;
  wire [2:0] aluop;
  wire [4:0] InSpliter_rd, InSpliter_rs, InSpliter_rt;
  wire [5:0] InSpliter_func, InSpliter_spec;
  wire [15:0] InSpliter_imm;
  wire [31:0] bit_extender_1_out, grf_1_rd1, multiplexer_1_out, multiplexer_4_out, multiplexer_5_out,
       ram_1_data;

  Clock clock_1 (.out(clk));
  IFU ifu_1 (.clk(clk), .reset(in_1), .branch(and_1_out), .imm(InSpliter_imm), .ins(out_2), .out_6(out_3));
  Multiplexer #(.width(32)) multiplexer_1 (
    .in0(out_8), .in1({InSpliter_imm, {16{1'b0}}}), .out(multiplexer_1_out), .sel(regW_src));  // open: en
  Multiplexer #(.width(32)) multiplexer_2 (
    .in0(multiplexer_1_out), .in1(ram_1_data), .out(out_6), .sel(memToReg));  // open: en
  break_Ins InSpliter (
    .in_1(out_2), .spec(InSpliter_spec), .rs(InSpliter_rs), .rt(InSpliter_rt), .rd(InSpliter_rd),
    .func(InSpliter_func), .imm(InSpliter_imm));  // open: _0
  and and_1 (and_1_out, inid_1_beq, alu_1_equal);
  Multiplexer #(.width(5)) multiplexer_3 (
    .in0(InSpliter_rd), .in1(InSpliter_rt), .out(out_5), .sel(control_unit_reg_dst));  // open: en
  inId inid_1 (
    .add(inid_1_add), .sub(inid_1_sub), .sll(inid_1_sll), .ori(inid_1_ori), .lw(inid_1_lw), .sw(inid_1_sw),
    .beq(inid_1_beq), .lui(inid_1_lui), .opcode(InSpliter_spec), .func(InSpliter_func));
  control control_unit (
    .regW(out_4), .reg_Dst(control_unit_reg_dst), .regW_src(regW_src), .memW(out_7), .memToReg(memToReg),
    .AluOp(aluop), .ext_way(control_unit_ext_way), .AluSrc1(control_unit_alusrc1),
    .AluSrc2(control_unit_alusrc2), .add(inid_1_add), .sub(inid_1_sub), .sll(inid_1_sll), .ori(inid_1_ori),
    .lw(inid_1_lw), .sw(inid_1_sw), .beq(inid_1_beq), .lui(inid_1_lui));
  grf grf_1 (
    .RA1(InSpliter_rs), .RA2(InSpliter_rt), .WA(out_5), .WD(out_6), .RD1(grf_1_rd1), .RD2(out_9), .clk(clk),
    .Reset(in_1), .WE(out_4));
  and and_2 (and_2_out, control_unit_ext_way, InSpliter_imm[15]);
  // Probe on grf_1_rd1
  assign bit_extender_1_out = {{16{and_2_out}}, InSpliter_imm};  // Bit_Extender bit_extender_1
  // Probe on multiplexer_4_out
  Multiplexer #(.width(32)) multiplexer_4 (
    .in0(grf_1_rd1), .in1(grf_1_rd1), .out(multiplexer_4_out), .sel(control_unit_alusrc1));  // open: en
  Multiplexer #(.width(32)) multiplexer_5 (
    .in0(out_9), .in1(bit_extender_1_out), .out(multiplexer_5_out), .sel(control_unit_alusrc2));  // open: en
  // Probe on multiplexer_5_out
  ALU alu_1 (.In1(multiplexer_4_out), .In2(multiplexer_5_out), .Out(out_8), .ALUop(aluop), .equal(alu_1_equal));
  RAM #(.addrWidth(12), .dataWidth(32), .bus("separate")) ram_1 (
    .addr(out_8[13:2]), .din(out_9), .data(ram_1_data), .str(out_7), .clk(clk), .ld(1'b1), .clr(in_1));  // open: sel

  // Other names for the same wires on the sheet: alu_out[31:0] = out_8; Instr[31:0] = out_2; MemData[31:0] = out_9;
  //   memW = out_7; PC[31:0] = out_3; regAdd[4:0] = out_5; regData[31:0] = out_6; regW = out_4; reset = in_1
endmodule

// Grf
module grf (
  input  clk,
  input  Reset,
  input  WE,
  input  [4:0] RA1,
  input  [4:0] RA2,
  input  [4:0] WA,
  input  [31:0] WD,
  output [31:0] RD1,
  output [31:0] RD2
);

  wire [31:0] _0, _1, _2, _3, _4, _5, _6, _7, _8, _9, _10, _11, _12, _13, _14, _15, _16, _17, _18, _19, _20,
       _21, _22, _23, _24, _25, _26, _27, _28, _29, _30, _31, I0, I1, I2, I3, I4, I5, I6, I7, I8, I9, I10,
       I11, I12, I13, I14, I15, I16, I17, I18, I19, I20, I21, I22, I23, I24, I25, I26, I27, I28, I29, I30,
       I31;

  Multiplexer #(.select(5), .width(32)) multiplexer_1 (
    .in0(_0), .in1(_1), .in2(_2), .in3(_3), .in4(_4), .in5(_5), .in6(_6), .in7(_7), .in8(_8), .in9(_9),
    .in10(_10), .in11(_11), .in12(_12), .in13(_13), .in14(_14), .in15(_15), .in16(_16), .in17(_17),
    .in18(_18), .in19(_19), .in20(_20), .in21(_21), .in22(_22), .in23(_23), .in24(_24), .in25(_25),
    .in26(_26), .in27(_27), .in28(_28), .in29(_29), .in30(_30), .in31(_31), .out(RD1), .sel(RA1));  // open: en
  Demultiplexer #(.select(5), .width(32), .tristate("true")) demultiplexer_1 (
    .out0(I0), .out1(I1), .out2(I2), .out3(I3), .out4(I4), .out5(I5), .out6(I6), .out7(I7), .out8(I8),
    .out9(I9), .out10(I10), .out11(I11), .out12(I12), .out13(I13), .out14(I14), .out15(I15), .out16(I16),
    .out17(I17), .out18(I18), .out19(I19), .out20(I20), .out21(I21), .out22(I22), .out23(I23), .out24(I24),
    .out25(I25), .out26(I26), .out27(I27), .out28(I28), .out29(I29), .out30(I30), .out31(I31), .in(WD),
    .sel(WA), .en(WE));
  Multiplexer #(.select(5), .width(32)) multiplexer_2 (
    .in0(_0), .in1(_1), .in2(_2), .in3(_3), .in4(_4), .in5(_5), .in6(_6), .in7(_7), .in8(_8), .in9(_9),
    .in10(_10), .in11(_11), .in12(_12), .in13(_13), .in14(_14), .in15(_15), .in16(_16), .in17(_17),
    .in18(_18), .in19(_19), .in20(_20), .in21(_21), .in22(_22), .in23(_23), .in24(_24), .in25(_25),
    .in26(_26), .in27(_27), .in28(_28), .in29(_29), .in30(_30), .in31(_31), .out(RD2), .sel(RA2));  // open: en
  // Probe on I1
  Register #(.width(32)) register_1 (.D(I0), .en(WE), .Q(_0), .clk(clk), .clr(1'b1));
  Register #(.width(32)) register_2 (.D(I6), .en(WE), .Q(_6), .clk(clk), .clr(Reset));
  Register #(.width(32)) register_3 (.D(I12), .en(WE), .Q(_12), .clk(clk), .clr(Reset));
  Register #(.width(32)) register_4 (.D(I18), .en(WE), .Q(_18), .clk(clk), .clr(Reset));
  Register #(.width(32)) register_5 (.D(I24), .en(WE), .Q(_24), .clk(clk), .clr(Reset));
  Register #(.width(32)) register_6 (.D(I30), .en(WE), .Q(_30), .clk(clk), .clr(Reset));
  // Probe on _1
  Register #(.width(32)) register_7 (.D(I1), .en(WE), .Q(_1), .clk(clk), .clr(Reset));
  Register #(.width(32)) register_8 (.D(I7), .en(WE), .Q(_7), .clk(clk), .clr(Reset));
  Register #(.width(32)) register_9 (.D(I13), .en(WE), .Q(_13), .clk(clk), .clr(Reset));
  Register #(.width(32)) register_10 (.D(I19), .en(WE), .Q(_19), .clk(clk), .clr(Reset));
  Register #(.width(32)) register_11 (.D(I25), .en(WE), .Q(_25), .clk(clk), .clr(Reset));
  Register #(.width(32)) register_12 (.D(I31), .en(WE), .Q(_31), .clk(clk), .clr(Reset));
  Register #(.width(32)) register_13 (.D(I2), .en(WE), .Q(_2), .clk(clk), .clr(Reset));
  Register #(.width(32)) register_14 (.D(I8), .en(WE), .Q(_8), .clk(clk), .clr(Reset));
  Register #(.width(32)) register_15 (.D(I14), .en(WE), .Q(_14), .clk(clk), .clr(Reset));
  Register #(.width(32)) register_16 (.D(I20), .en(WE), .Q(_20), .clk(clk), .clr(Reset));
  Register #(.width(32)) register_17 (.D(I26), .en(WE), .Q(_26), .clk(clk), .clr(Reset));
  Register #(.width(32)) register_18 (.D(I3), .en(WE), .Q(_3), .clk(clk), .clr(Reset));
  Register #(.width(32)) register_19 (.D(I9), .en(WE), .Q(_9), .clk(clk), .clr(Reset));
  Register #(.width(32)) register_20 (.D(I15), .en(WE), .Q(_15), .clk(clk), .clr(Reset));
  Register #(.width(32)) register_21 (.D(I21), .en(WE), .Q(_21), .clk(clk), .clr(Reset));
  Register #(.width(32)) register_22 (.D(I27), .en(WE), .Q(_27), .clk(clk), .clr(Reset));
  Register #(.width(32)) register_23 (.D(I4), .en(WE), .Q(_4), .clk(clk), .clr(Reset));
  Register #(.width(32)) register_24 (.D(I10), .en(WE), .Q(_10), .clk(clk), .clr(Reset));
  Register #(.width(32)) register_25 (.D(I16), .en(WE), .Q(_16), .clk(clk), .clr(Reset));
  Register #(.width(32)) register_26 (.D(I22), .en(WE), .Q(_22), .clk(clk), .clr(Reset));
  Register #(.width(32)) register_27 (.D(I28), .en(WE), .Q(_28), .clk(clk), .clr(Reset));
  Register #(.width(32)) register_28 (.D(I5), .en(WE), .Q(_5), .clk(clk), .clr(Reset));
  Register #(.width(32)) register_29 (.D(I11), .en(WE), .Q(_11), .clk(clk), .clr(Reset));
  Register #(.width(32)) register_30 (.D(I17), .en(WE), .Q(_17), .clk(clk), .clr(Reset));
  Register #(.width(32)) register_31 (.D(I23), .en(WE), .Q(_23), .clk(clk), .clr(Reset));
  Register #(.width(32)) register_32 (.D(I29), .en(WE), .Q(_29), .clk(clk), .clr(Reset));

  // Other names for the same wires on the sheet: A1[4:0] = RA1; A2[4:0] = RA2; A3[4:0] = WA
endmodule

module ALU (
  input  [31:0] In1,
  input  [31:0] In2,
  input  [2:0] ALUop,
  output equal,
  output [31:0] Out
);

  wire [31:0] adder_1_out, multiplier_1_out, or_1_out, subtractor_1_out;

  Adder #(.width(32)) adder_1 (.a(In1), .b(In2), .out(adder_1_out));  // open: cin, cout
  Subtractor #(.width(32)) subtractor_1 (.a(In1), .b(In2), .out(subtractor_1_out));  // open: bin, bout
  Multiplier #(.width(32)) multiplier_1 (.a(In1), .b(In2), .out(multiplier_1_out));  // open: cin, cout
  assign or_1_out = In1 | In2;  // OR_Gate or_1, 32 bits wide
  Comparator #(.width(32)) comparator_1 (.a(In1), .b(In2), .eq(equal));  // open: gt, lt
  Multiplexer #(.select(3), .width(32)) multiplexer_1 (
    .in0(adder_1_out), .in1(subtractor_1_out), .in2(multiplier_1_out), .in3(or_1_out), .in4({32{1'b0}}),
    .in5({32{1'b0}}), .in6({32{1'b0}}), .in7({32{1'b0}}), .out(Out), .sel(ALUop));  // open: en
endmodule

module break_Ins (
  input  [31:0] in_1,
  output [5:0] spec,
  output [4:0] rs,
  output [4:0] rt,
  output [4:0] rd,
  output [4:0] _0,
  output [5:0] func,
  output [15:0] imm
);


  assign _0 = in_1[10:6];
  assign func = in_1[5:0];
  assign imm = in_1[15:0];
  assign rd = in_1[15:11];
  assign rs = in_1[25:21];
  assign rt = in_1[20:16];
  assign spec = in_1[31:26];
endmodule

module inId (
  input  [5:0] opcode,
  input  [5:0] func,
  output add,
  output sub,
  output sll,
  output ori,
  output lw,
  output sw,
  output beq,
  output lui
);

  wire is_R;

  and and_1 (is_R, ~opcode[5], ~opcode[4], ~opcode[3], ~opcode[2], ~opcode[1], ~opcode[0]);  // AND_Gate
  and and_2 (add, is_R, func[5], ~func[4], ~func[3], ~func[2], ~func[1], ~func[0]);  // AND_Gate
  and and_3 (sub, is_R, func[5], ~func[4], ~func[3], ~func[2], func[1], ~func[0]);  // AND_Gate
  and and_4 (sll, is_R, ~func[5], ~func[4], ~func[3], ~func[2], ~func[1], ~func[0]);  // AND_Gate
  and and_5 (ori, ~opcode[5], ~opcode[4], opcode[3], opcode[2], ~opcode[1], opcode[0]);  // AND_Gate
  and and_6 (lw, opcode[5], ~opcode[4], ~opcode[3], ~opcode[2], opcode[1], opcode[0]);  // AND_Gate
  and and_7 (sw, opcode[5], ~opcode[4], opcode[3], ~opcode[2], opcode[1], opcode[0]);  // AND_Gate
  and and_8 (beq, ~opcode[5], ~opcode[4], ~opcode[3], opcode[2], ~opcode[1], ~opcode[0]);  // AND_Gate
  and and_9 (lui, ~opcode[5], ~opcode[4], opcode[3], opcode[2], opcode[1], opcode[0]);  // AND_Gate
endmodule

module control (
  input  add,
  input  sub,
  input  sll,
  input  ori,
  input  lw,
  input  sw,
  input  beq,
  input  lui,
  output regW,
  output reg_Dst,
  output regW_src,
  output memW,
  output memToReg,
  output [2:0] AluOp,
  output ext_way,
  output AluSrc1,
  output AluSrc2
);

  wire [2:0] multiplexer_1_out, multiplexer_2_out;

  Multiplexer #(.width(3)) multiplexer_1 (.in0(3'b000), .in1(3'b001), .out(multiplexer_1_out), .sel(sub));  // open: en
  or or_1 (regW, add, sub, ori, lw, lui);
  or or_2 (reg_Dst, ori, lw, lui);
  or or_3 (ext_way, beq, sw, lw);
  or or_4 (AluSrc2, ori, lw, sw);
  Multiplexer #(.width(3)) multiplexer_2 (
    .in0(multiplexer_1_out), .in1(3'b011), .out(multiplexer_2_out), .sel(ori));  // open: en
  Multiplexer #(.width(3)) multiplexer_3 (.in0(multiplexer_2_out), .in1(3'b100), .out(AluOp), .sel(lui));  // open: en

  assign AluSrc1 = sll;
  assign memToReg = lw;
  assign memW = sw;
  assign regW_src = lui;
endmodule

module IFU (
  input  clk,
  input  reset,
  input  branch,
  input  [15:0] imm,
  output [31:0] ins,
  output [31:0] out_6
);

  wire [31:0] adder_1_out, adder_2_out, bit_extender_1_out, multiplexer_1_out, PC_q, shifter_1_out,
       subtractor_1_out, xor_1_out;

  // Probe on multiplexer_1_out
  Multiplexer #(.width(32)) multiplexer_1 (
    .in0(adder_1_out), .in1(adder_2_out), .out(multiplexer_1_out), .sel(branch));  // open: en
  assign xor_1_out = 32'h3000 ^ multiplexer_1_out;  // XOR_Gate xor_1, 32 bits wide
  Register #(.width(32)) PC (.D(xor_1_out), .Q(PC_q), .clk(clk), .clr(reset));  // open: en
  assign out_6 = 32'h3000 ^ PC_q;  // XOR_Gate xor_2, 32 bits wide
  Adder #(.width(32)) adder_1 (.a(out_6), .b(32'h4), .out(adder_1_out));  // open: cin, cout
  assign bit_extender_1_out = {{16{imm[15]}}, imm};  // Bit_Extender bit_extender_1
  Shifter #(.width(32)) shifter_1 (.in(bit_extender_1_out), .\dist (5'b00010), .out(shifter_1_out));
  Subtractor #(.width(32)) subtractor_1 (.a(out_6), .b(32'h3000), .out(subtractor_1_out));  // open: bin, bout
  Adder #(.width(32)) adder_2 (.a(adder_1_out), .b(shifter_1_out), .out(adder_2_out));  // open: cin, cout
  ROM #(.addrWidth(12), .dataWidth(32)) rom_1 (.addr(subtractor_1_out[13:2]), .data(ins));  // open: sel

  // Other names for the same wires on the sheet: PC[31:0] = out_6

  // Notes on the sheet:
  //   contents of rom_1 (hex, n*v repeats v):
  //   341c0000 341d0000 34013456 210820 8c010004 ac010004 3c027878 411822 3c051234 34040005 0 ac85ffff
  //   8c83ffff 10650001 1000000d 34670404 10e3000b 0 3c087777 3508ffff 80022 34001100 e65020 34080000
  //   34090001 340a0001 10a4020 1109fffe 1000ffff
endmodule
