// Logisim project 4bit_sort.circ as structural Verilog: 3 circuits, main circuit 4bit_sort
module _4bit_sort (
  input  [3:0] A,
  input  [3:0] B,
  input  [3:0] C,
  input  [3:0] D,
  output [3:0] O1,
  output [3:0] O2,
  output [3:0] O3,
  output [3:0] O4
);

  wire comparator_1_gt, comparator_2_gt, comparator_3_gt, comparator_4_gt, comparator_5_gt, comparator_6_gt;
  wire [3:0] n4bit_swap_1_o1, n4bit_swap_1_o2, n4bit_swap_2_o1, n4bit_swap_2_o2, n4bit_swap_3_o1,
       n4bit_swap_3_o2, n4bit_swap_4_o2, n4bit_swap_5_o2;

  Comparator #(.width(4), .mode("unsigned")) comparator_1 (.a(C), .b(D), .gt(comparator_1_gt));  // open: eq, lt
  // Probe on n4bit_swap_1_o1
  _4bit_swap u_4bit_swap_1 (.I1(C), .I2(D), .O1(n4bit_swap_1_o1), .O2(n4bit_swap_1_o2), .S(comparator_1_gt));
  // Probe on n4bit_swap_1_o2
  Comparator #(.width(4), .mode("unsigned")) comparator_2 (
    .a(n4bit_swap_2_o2), .b(n4bit_swap_1_o2), .gt(comparator_2_gt));  // open: eq, lt
  // Probe on B
  Comparator #(.width(4), .mode("unsigned")) comparator_3 (
    .a(n4bit_swap_1_o1), .b(B), .gt(comparator_3_gt));  // open: eq, lt
  // Probe on n4bit_swap_2_o1
  _4bit_swap u_4bit_swap_2 (
    .I1(n4bit_swap_1_o1), .I2(B), .O1(n4bit_swap_2_o1), .O2(n4bit_swap_2_o2), .S(comparator_3_gt));
  // Probe on n4bit_swap_2_o2
  _4bit_swap u_4bit_swap_3 (
    .I1(n4bit_swap_2_o2), .I2(n4bit_swap_1_o2), .O1(n4bit_swap_3_o1), .O2(n4bit_swap_3_o2),
    .S(comparator_2_gt));
  Comparator #(.width(4), .mode("unsigned")) comparator_4 (
    .a(n4bit_swap_2_o1), .b(A), .gt(comparator_4_gt));  // open: eq, lt
  Comparator #(.width(4), .mode("unsigned")) comparator_5 (
    .a(n4bit_swap_4_o2), .b(n4bit_swap_3_o1), .gt(comparator_5_gt));  // open: eq, lt
  Comparator #(.width(4), .mode("unsigned")) comparator_6 (
    .a(n4bit_swap_5_o2), .b(n4bit_swap_3_o2), .gt(comparator_6_gt));  // open: eq, lt
  _4bit_swap u_4bit_swap_4 (.I1(n4bit_swap_2_o1), .I2(A), .O1(O1), .O2(n4bit_swap_4_o2), .S(comparator_4_gt));
  _4bit_swap u_4bit_swap_5 (
    .I1(n4bit_swap_4_o2), .I2(n4bit_swap_3_o1), .O1(O2), .O2(n4bit_swap_5_o2), .S(comparator_5_gt));
  _4bit_swap u_4bit_swap_6 (.I1(n4bit_swap_5_o2), .I2(n4bit_swap_3_o2), .O1(O3), .O2(O4), .S(comparator_6_gt));
endmodule

module _1bit_swap (
  input  S,
  input  I1,
  input  I2,
  output O1,
  output O2
);

  wire and_1_out, and_2_out, and_3_out, and_4_out, not_1_out, not_2_out;

  not not_1 (not_1_out, S);
  not not_2 (not_2_out, S);
  and and_1 (and_1_out, not_1_out, I1);
  and and_2 (and_2_out, S, I2);
  and and_3 (and_3_out, not_2_out, I2);
  and and_4 (and_4_out, S, I1);
  or or_1 (O1, and_1_out, and_2_out);
  or or_2 (O2, and_3_out, and_4_out);
endmodule

module _4bit_swap (
  input  S,
  input  [3:0] I1,
  input  [3:0] I2,
  output [3:0] O1,
  output [3:0] O2
);

  _1bit_swap u_1bit_swap_1 (.S(S), .I1(I1[0]), .I2(I2[0]), .O1(O1[0]), .O2(O2[0]));
  _1bit_swap u_1bit_swap_2 (.S(S), .I1(I1[1]), .I2(I2[1]), .O1(O1[1]), .O2(O2[1]));
  _1bit_swap u_1bit_swap_3 (.S(S), .I1(I1[2]), .I2(I2[2]), .O1(O1[2]), .O2(O2[2]));
  _1bit_swap u_1bit_swap_4 (.S(S), .I1(I1[3]), .I2(I2[3]), .O1(O1[3]), .O2(O2[3]));

  // Other names for the same wires on the sheet: _10 = I1[0]; _11 = I1[1]; _12 = I1[2]; _13 = I1[3]; _20 = I2[0];
  //   _21 = I2[1]; _22 = I2[2]; _23 = I2[3]
endmodule
