// Logisim project CRC.circ as structural Verilog: 2 circuits, main circuit CRC
module CRC (
  input  [7:0] A,
  input  [3:0] B,
  output [10:0] O
);

  wire [2:0] mod4_1_out, mod4_2_out, mod4_3_out, mod4_4_out, mod4_5_out, mod4_6_out, mod4_7_out;

  // Probe on A[7:4]
  // Probe on mod4_1_out
  mod4 mod4_1 (.A(A[7:4]), .B(B), .out(mod4_1_out));
  // Probe on {mod4_1_out, A[3]}
  mod4 mod4_2 (.A({mod4_1_out, A[3]}), .B(B), .out(mod4_2_out));
  // Probe on {mod4_2_out, A[2]}
  mod4 mod4_3 (.A({mod4_2_out, A[2]}), .B(B), .out(mod4_3_out));
  // Probe on {mod4_3_out, A[1]}
  mod4 mod4_4 (.A({mod4_3_out, A[1]}), .B(B), .out(mod4_4_out));
  mod4 mod4_5 (.A({mod4_4_out, A[0]}), .B(B), .out(mod4_5_out));
  mod4 mod4_6 (.A({mod4_5_out, 1'b0}), .B(B), .out(mod4_6_out));
  mod4 mod4_7 (.A({mod4_6_out, 1'b0}), .B(B), .out(mod4_7_out));
  mod4 mod4_8 (.A({mod4_7_out, 1'b0}), .B(B), .out(O[2:0]));

  assign O[10:3] = A;

  // Other names for the same wires on the sheet: out[2:0] = O[2:0]
endmodule

module mod4 (
  input  [3:0] A,
  input  [3:0] B,
  output [2:0] out
);

  wire [3:0] xor_1_out, xor_2_out;

  assign xor_1_out = A ^ B;  // XOR_Gate xor_1, 4 bits wide
  assign xor_2_out = A ^ 4'b0000;  // XOR_Gate xor_2, 4 bits wide
  // Probe on xor_1_out
  Multiplexer #(.width(3)) multiplexer_1 (
    .in0(xor_2_out[2:0]), .in1(xor_1_out[2:0]), .out(out), .sel(A[3]));  // open: en
endmodule
