// Logisim project fib1.circ as structural Verilog: 3 circuits, main circuit count
module count (
  input  [2:0] INPUT,
  output OUTPUT_SIGN
);

  wire clock_1_out, comparator_1_eq, comparator_1_lt;
  wire [3:0] adder_1_out, bit_extender_1_out, counter_1_q;

  Clock clock_1 (.out(clock_1_out));
  Counter #(.width(4), .max('h8), .ongoal("stay")) counter_1 (
    .Q(counter_1_q), .clk(clock_1_out));  // open: load, D, count, carry, clr
  assign bit_extender_1_out = {{1{1'b0}}, INPUT};  // Bit_Extender bit_extender_1
  Adder #(.width(4)) adder_1 (.a(4'b0001), .b(bit_extender_1_out), .out(adder_1_out));  // open: cin, cout
  Comparator #(.width(4), .mode("unsigned")) comparator_1 (
    .a(adder_1_out), .b(counter_1_q), .eq(comparator_1_eq), .lt(comparator_1_lt));  // open: gt
  or or_1 (OUTPUT_SIGN, comparator_1_eq, comparator_1_lt);
endmodule

module main (
  input  [2:0] INPUT,
  output [3:0] out_2
);

  wire count_1_output_sign;
  wire [3:0] work_1_out_2;

  count count_1 (.INPUT(INPUT), .OUTPUT_SIGN(count_1_output_sign));
  // Probe on count_1_output_sign
  work work_1 (.in_1(count_1_output_sign), .out_2(work_1_out_2));
  Multiplexer #(.width(4)) multiplexer_1 (
    .in0(4'b0000), .in1(work_1_out_2), .out(out_2), .sel(count_1_output_sign));  // open: en
  // Probe on work_1_out_2
endmodule

module work (
  input  in_1,
  output [3:0] out_2
);

  wire CLOCK, counter_1_q, Freeze;
  wire [3:0] adder_1_out, multiplexer_1_out, Pre;

  Clock clock_1 (.out(CLOCK));
  not not_1 (Freeze, in_1);
  Counter #(.width(1), .max('h1), .ongoal("stay")) counter_1 (
    .Q(counter_1_q), .clk(CLOCK));  // open: load, D, count, carry, clr
  Adder #(.width(4)) adder_1 (.a(out_2), .b(Pre), .out(adder_1_out));  // open: cin, cout
  Multiplexer #(.width(4)) multiplexer_1 (
    .in0(4'b0001), .in1(out_2), .out(multiplexer_1_out), .sel(counter_1_q));  // open: en
  Register #(.width(4)) u_Pre (.D(multiplexer_1_out), .en(Freeze), .Q(Pre), .clk(CLOCK));  // open: clr
  Register #(.width(4)) Now (.D(adder_1_out), .en(Freeze), .Q(out_2), .clk(CLOCK));  // open: clr

  // Other names for the same wires on the sheet: Now[3:0] = out_2
endmodule
