// Logisim project fib2.circ as structural Verilog: 8 circuits, main circuit main
module main (
  input  [31:0] in_1,
  output [31:0] out_2
);

  wire work_freeze;
  wire [31:0] out11, out12, out21, out22;

  \计数  work (.in_1(in_1), .freeze(work_freeze), .out_3(out11), .out_4(out21), .out_5(out12), .out_6(out22));
  // Probe on out11
  // Probe on out12
  Multiplexer #(.width(32)) multiplexer_1 (.in0({32{1'b0}}), .in1(out12), .out(out_2), .sel(work_freeze));  // open: en
  // Probe on out21
  // Probe on out22
endmodule

// 选择
module \计数  (
  input  [31:0] in_1,
  output freeze,
  output [31:0] out_3,
  output [31:0] out_4,
  output [31:0] out_5,
  output [31:0] out_6
);

  wire Clock, comparator_1_eq, counter_1_q, counter_3_q, \initial , low, multiplexer_2_out;
  wire [31:0] a11, a12, a21, a22, multiplexer_1_out, now_num, register_1_q, select_1_out_10, select_1_out_11,
       select_1_out_12, select_1_out_13, select_2_out_10, select_2_out_11, select_2_out_12, select_2_out_13,
       \元矩阵_1_s11 , \元矩阵_1_s12 , \元矩阵_1_s21 , \元矩阵_1_s22 , \元矩阵_2_s11 , \元矩阵_2_s12 , \元矩阵_2_s21 ,
       \元矩阵_2_s22 , \初始矩阵_1_s11 , \初始矩阵_1_s12 , \初始矩阵_1_s21 , \初始矩阵_1_s22 , \矩阵乘法_1_out11 , \矩阵乘法_1_out12 ,
       \矩阵乘法_1_out21 , \矩阵乘法_1_out22 , \矩阵乘法_2_out11 , \矩阵乘法_2_out12 , \矩阵乘法_2_out21 , \矩阵乘法_2_out22 ,
       \选择_out_10 , \选择_out_11 , \选择_out_12 , \选择_out_13 ;

  Clock clock_1 (.out(Clock));
  Counter #(.width(1), .max('h1), .ongoal("stay")) counter_1 (
    .Q(counter_1_q), .clk(Clock));  // open: load, D, count, carry, clr
  Multiplexer #(.width(32)) multiplexer_1 (
    .in0(in_1), .in1(now_num), .out(multiplexer_1_out), .sel(counter_1_q));  // open: en
  \矩阵乘法  \u_矩阵乘法_1  (
    .in_1(a11), .in_2(a11), .in_3(a12), .in_4(a12), .in_5(a21), .in_6(a21), .in_7(a22), .in_8(a22),
    .out11(\矩阵乘法_1_out11 ), .out12(\矩阵乘法_1_out12 ), .out21(\矩阵乘法_1_out21 ), .out22(\矩阵乘法_1_out22 ));
  Register #(.width(32)) register_1 (.D(multiplexer_1_out), .Q(register_1_q), .clk(Clock));  // open: en, clr
  // Probe on now_num
  \初始矩阵  \u_初始矩阵_1  (.s11(\初始矩阵_1_s11 ), .s12(\初始矩阵_1_s12 ), .s21(\初始矩阵_1_s21 ), .s22(\初始矩阵_1_s22 ));
  select select_1 (
    .flag(\initial ), .v11(\初始矩阵_1_s11 ), .in_3(\矩阵乘法_1_out11 ), .v12(\初始矩阵_1_s12 ), .in_5(\矩阵乘法_1_out12 ),
    .v21(\初始矩阵_1_s21 ), .in_7(\矩阵乘法_1_out21 ), .v22(\初始矩阵_1_s22 ), .in_9(\矩阵乘法_1_out22 ),
    .out_10(select_1_out_10), .out_11(select_1_out_11), .out_12(select_1_out_12), .out_13(select_1_out_13));
  // Probe on low
  Bit_Extender #(.in_width(32), .out_width(1)) bit_extender_1 (.in(register_1_q), .out(low));
  Shifter #(.width(32), .shift("lr")) shifter_1 (.in(register_1_q), .\dist (5'b00001), .out(now_num));
  // Probe on now_num
  ans ans_1 (
    .in_1(freeze), .In11(select_1_out_10), .In21(select_1_out_12), .In12(select_1_out_11),
    .In22(select_1_out_13), .out_6(a11), .out_7(a12), .out_8(a21), .out_9(a22));
  \元矩阵  \u_元矩阵_1  (.s11(\元矩阵_1_s11 ), .s12(\元矩阵_1_s12 ), .s21(\元矩阵_1_s21 ), .s22(\元矩阵_1_s22 ));
  Counter #(.width(1), .max('h1), .ongoal("stay")) counter_2 (
    .Q(\initial ), .clk(Clock));  // open: load, D, count, carry, clr
  select \u_选择  (
    .flag(low), .v11(\元矩阵_1_s11 ), .in_3(a11), .v12(\元矩阵_1_s12 ), .in_5(a12), .v21(\元矩阵_1_s21 ), .in_7(a21),
    .v22(\元矩阵_1_s22 ), .in_9(a22), .out_10(\选择_out_10 ), .out_11(\选择_out_11 ), .out_12(\选择_out_12 ),
    .out_13(\选择_out_13 ));
  Comparator #(.width(32)) comparator_1 (.a(now_num), .b({32{1'b0}}), .eq(comparator_1_eq));  // open: gt, lt
  Counter #(.width(1), .max('h1), .ongoal("stay")) counter_3 (
    .Q(counter_3_q), .clk(Clock));  // open: load, D, count, carry, clr
  Multiplexer multiplexer_2 (
    .in0(1'b0), .in1(comparator_1_eq), .out(multiplexer_2_out), .sel(counter_3_q));  // open: en
  \元矩阵  \u_元矩阵_2  (.s11(\元矩阵_2_s11 ), .s12(\元矩阵_2_s12 ), .s21(\元矩阵_2_s21 ), .s22(\元矩阵_2_s22 ));
  \矩阵乘法  \u_矩阵乘法_2  (
    .in_1(out_3), .in_2(\选择_out_10 ), .in_3(out_5), .in_4(\选择_out_11 ), .in_5(out_4), .in_6(\选择_out_12 ),
    .in_7(out_6), .in_8(\选择_out_13 ), .out11(\矩阵乘法_2_out11 ), .out12(\矩阵乘法_2_out12 ), .out21(\矩阵乘法_2_out21 ),
    .out22(\矩阵乘法_2_out22 ));
  Register #(.width(1)) register_2 (.D(multiplexer_2_out), .Q(freeze), .clk(Clock));  // open: en, clr
  select select_2 (
    .flag(\initial ), .v11(\元矩阵_2_s11 ), .in_3(\矩阵乘法_2_out11 ), .v12(\元矩阵_2_s12 ), .in_5(\矩阵乘法_2_out12 ),
    .v21(\元矩阵_2_s21 ), .in_7(\矩阵乘法_2_out21 ), .v22(\元矩阵_2_s22 ), .in_9(\矩阵乘法_2_out22 ),
    .out_10(select_2_out_10), .out_11(select_2_out_11), .out_12(select_2_out_12), .out_13(select_2_out_13));
  \tmp矩阵  tmp (
    .in_1(freeze), .In11(select_2_out_10), .In12(select_2_out_11), .In22(select_2_out_13), .out_6(out_3),
    .out_7(out_5), .out_8(out_4), .out_9(out_6), .In21(select_2_out_12));

  // Other names for the same wires on the sheet: Input[31:0] = in_1; out11[31:0] = out_3; out12[31:0] = out_5;
  //   out21[31:0] = out_4; out22[31:0] = out_6
endmodule

// 乘法器
module \矩阵乘法  (
  input  [31:0] in_1,
  input  [31:0] in_2,
  input  [31:0] in_3,
  input  [31:0] in_4,
  input  [31:0] in_5,
  input  [31:0] in_6,
  input  [31:0] in_7,
  input  [31:0] in_8,
  output [31:0] out11,
  output [31:0] out12,
  output [31:0] out21,
  output [31:0] out22
);

  wire [31:0] multiplier_1_out, multiplier_2_out, multiplier_3_out, multiplier_4_out, multiplier_5_out,
       multiplier_6_out, multiplier_7_out, multiplier_8_out;

  Multiplier #(.width(32)) multiplier_1 (.a(in_1), .b(in_2), .out(multiplier_1_out));  // open: cin, cout
  Multiplier #(.width(32)) multiplier_2 (.a(in_3), .b(in_6), .out(multiplier_2_out));  // open: cin, cout
  Multiplier #(.width(32)) multiplier_3 (.a(in_1), .b(in_4), .out(multiplier_3_out));  // open: cin, cout
  Multiplier #(.width(32)) multiplier_4 (.a(in_3), .b(in_8), .out(multiplier_4_out));  // open: cin, cout
  Multiplier #(.width(32)) multiplier_5 (.a(in_5), .b(in_2), .out(multiplier_5_out));  // open: cin, cout
  Multiplier #(.width(32)) multiplier_6 (.a(in_7), .b(in_6), .out(multiplier_6_out));  // open: cin, cout
  Multiplier #(.width(32)) multiplier_7 (.a(in_5), .b(in_4), .out(multiplier_7_out));  // open: cin, cout
  Multiplier #(.width(32)) multiplier_8 (.a(in_7), .b(in_8), .out(multiplier_8_out));  // open: cin, cout
  Adder #(.width(32)) adder_1 (.a(multiplier_1_out), .b(multiplier_2_out), .out(out11));  // open: cin, cout
  Adder #(.width(32)) adder_2 (.a(multiplier_3_out), .b(multiplier_4_out), .out(out12));  // open: cin, cout
  Adder #(.width(32)) adder_3 (.a(multiplier_5_out), .b(multiplier_6_out), .out(out21));  // open: cin, cout
  Adder #(.width(32)) adder_4 (.a(multiplier_7_out), .b(multiplier_8_out), .out(out22));  // open: cin, cout

  // Other names for the same wires on the sheet: a11[31:0] = in_1; a12[31:0] = in_3; a21[31:0] = in_5;
  //   a22[31:0] = in_7; b11[31:0] = in_2; b12[31:0] = in_4; b21[31:0] = in_6; b22[31:0] = in_8
endmodule

module \元矩阵  (
  output [31:0] s11,
  output [31:0] s12,
  output [31:0] s21,
  output [31:0] s22
);


  assign s11 = 32'h1;
  assign s12 = {32{1'b0}};
  assign s21 = {32{1'b0}};
  assign s22 = 32'h1;
endmodule

module ans (
  input  in_1,
  input  [31:0] In11,
  input  [31:0] In21,
  input  [31:0] In12,
  input  [31:0] In22,
  output [31:0] out_6,
  output [31:0] out_7,
  output [31:0] out_8,
  output [31:0] out_9
);

  wire clock_1_out, clock_2_out, clock_3_out, clock_4_out, ena;

  not not_1 (ena, in_1);
  Register #(.width(32)) register_1 (.D(In11), .en(ena), .Q(out_6), .clk(clock_1_out));  // open: clr
  Clock clock_1 (.out(clock_1_out));
  Register #(.width(32)) register_2 (.D(In12), .en(ena), .Q(out_7), .clk(clock_2_out));  // open: clr
  Clock clock_2 (.out(clock_2_out));
  Register #(.width(32)) register_3 (.D(In21), .en(ena), .Q(out_8), .clk(clock_3_out));  // open: clr
  Clock clock_3 (.out(clock_3_out));
  Register #(.width(32)) register_4 (.D(In22), .en(ena), .Q(out_9), .clk(clock_4_out));  // open: clr
  Clock clock_4 (.out(clock_4_out));

  // Other names for the same wires on the sheet: out11[31:0] = out_6; out12[31:0] = out_7; out21[31:0] = out_8;
  //   out22[31:0] = out_9
endmodule

module select (
  input  flag,
  input  [31:0] v11,
  input  [31:0] in_3,
  input  [31:0] v12,
  input  [31:0] in_5,
  input  [31:0] v21,
  input  [31:0] in_7,
  input  [31:0] v22,
  input  [31:0] in_9,
  output [31:0] out_10,
  output [31:0] out_11,
  output [31:0] out_12,
  output [31:0] out_13
);

  Multiplexer #(.width(32)) multiplexer_1 (.in0(v11), .in1(in_3), .out(out_10), .sel(flag));  // open: en
  Multiplexer #(.width(32)) multiplexer_2 (.in0(v12), .in1(in_5), .out(out_11), .sel(flag));  // open: en
  Multiplexer #(.width(32)) multiplexer_3 (.in0(v21), .in1(in_7), .out(out_12), .sel(flag));  // open: en
  Multiplexer #(.width(32)) multiplexer_4 (.in0(v22), .in1(in_9), .out(out_13), .sel(flag));  // open: en

  // Other names for the same wires on the sheet: out11[31:0] = out_10; out12[31:0] = out_11; out21[31:0] = out_12;
  //   out22[31:0] = out_13; s11[31:0] = v11; s12[31:0] = v12; s21[31:0] = v21; s22[31:0] = v22; v11_t[31:0] = in_3;
  //   v12_t[31:0] = in_5; v21_t[31:0] = in_7; v22_t[31:0] = in_9
endmodule

module \tmp矩阵  (
  input  in_1,
  input  [31:0] In11,
  input  [31:0] In21,
  input  [31:0] In12,
  input  [31:0] In22,
  output [31:0] out_6,
  output [31:0] out_7,
  output [31:0] out_8,
  output [31:0] out_9
);

  wire clock_1_out, clock_2_out, clock_3_out, clock_4_out, ena;

  not not_1 (ena, in_1);
  Clock clock_1 (.out(clock_1_out));
  Register #(.width(32)) register_1 (.D(In12), .en(ena), .Q(out_7), .clk(clock_2_out));  // open: clr
  Clock clock_2 (.out(clock_2_out));
  Register #(.width(32)) register_2 (.D(In11), .en(ena), .Q(out_6), .clk(clock_1_out));  // open: clr
  Register #(.width(32)) register_3 (.D(In21), .en(ena), .Q(out_8), .clk(clock_3_out));  // open: clr
  Clock clock_3 (.out(clock_3_out));
  Register #(.width(32)) register_4 (.D(In22), .en(ena), .Q(out_9), .clk(clock_4_out));  // open: clr
  Clock clock_4 (.out(clock_4_out));

  // Other names for the same wires on the sheet: out11[31:0] = out_6; out12[31:0] = out_7; out21[31:0] = out_8;
  //   out22[31:0] = out_9
endmodule

module \初始矩阵  (
  output [31:0] s11,
  output [31:0] s12,
  output [31:0] s21,
  output [31:0] s22
);


  assign s11 = 32'h1;
  assign s12 = 32'h1;
  assign s21 = 32'h1;
  assign s22 = {32{1'b0}};
endmodule
