// Logisim project fsm.circ as structural Verilog: 3 circuits, main circuit fsm
module fsm (
  input  CLR,
  input  [1:0] In,
  output out
);

  wire clk, comparator_1_eq, multiplexer_1_out, reset;
  wire [2:0] nextstate_1_out0, now;

  Clock clock_1 (.out(clk));
  Comparator #(.width(1), .mode("unsigned")) comparator_1 (.a(reset), .b(1'b1), .eq(comparator_1_eq));  // open: gt, lt
  nextstate nextstate_1 (
    .In1(In[1]), .In0(In[0]), .now2(now[2]), .now1(now[1]), .now0(now[0]), .out2(nextstate_1_out0[2]),
    .out1(nextstate_1_out0[1]), .out0(nextstate_1_out0[0]));
  Multiplexer multiplexer_1 (.in0(CLR), .in1(1'b0), .out(multiplexer_1_out), .sel(comparator_1_eq));  // open: en
  Register #(.width(1)) register_1 (.D(multiplexer_1_out), .Q(reset), .clk(clk));  // open: en, clr
  Register #(.width(3)) register_2 (.D(nextstate_1_out0), .Q(now), .clk(clk), .clr(reset));  // open: en
  // Probe on now
  judge judge_1 (.In1(In[1]), .In0(In[0]), .now2(now[2]), .now1(now[1]), .now0(now[0]), .out(out));
endmodule

module judge (
  input  In1,
  input  In0,
  input  now2,
  input  now1,
  input  now0,
  output out
);

  wire and_1_out, and_2_out, not_1_out, not_2_out, not_3_out, not_4_out, not_5_out;

  not not_1 (not_1_out, In0);
  not not_2 (not_2_out, now2);
  not not_3 (not_3_out, In0);
  not not_4 (not_4_out, now1);
  not not_5 (not_5_out, now0);
  and and_1 (and_1_out, not_1_out, not_2_out, now1, now0);
  and and_2 (and_2_out, not_3_out, now2, not_4_out, not_5_out);
  or or_1 (out, and_1_out, and_2_out);
endmodule

module nextstate (
  input  In1,
  input  In0,
  input  now2,
  input  now1,
  input  now0,
  output out2,
  output out1,
  output out0
);

  wire and_1_out, and_2_out, and_3_out, and_4_out, and_5_out, and_6_out, and_7_out, and_8_out, not_1_out,
       not_2_out, not_3_out, not_4_out, not_5_out, not_6_out, not_7_out, not_8_out, not_9_out, not_10_out,
       not_11_out, not_12_out, not_13_out, not_14_out, not_15_out, not_16_out, not_17_out, not_18_out,
       not_19_out, not_20_out, not_21_out, not_22_out, not_23_out, not_24_out, not_25_out;

  not not_1 (not_1_out, In0);
  not not_2 (not_2_out, now2);
  not not_3 (not_3_out, now1);
  not not_4 (not_4_out, In0);
  not not_5 (not_5_out, now2);
  not not_6 (not_6_out, now0);
  not not_7 (not_7_out, In1);
  not not_8 (not_8_out, now2);
  not not_9 (not_9_out, now1);
  not not_10 (not_10_out, In1);
  not not_11 (not_11_out, now2);
  not not_12 (not_12_out, now0);
  not not_13 (not_13_out, In1);
  not not_14 (not_14_out, In0);
  not not_15 (not_15_out, now2);
  not not_16 (not_16_out, now1);
  not not_17 (not_17_out, In1);
  not not_18 (not_18_out, In0);
  not not_19 (not_19_out, now2);
  not not_20 (not_20_out, now0);
  not not_21 (not_21_out, In1);
  not not_22 (not_22_out, now1);
  not not_23 (not_23_out, now0);
  not not_24 (not_24_out, In1);
  not not_25 (not_25_out, now2);
  and and_1 (and_1_out, In1, not_1_out, not_2_out, not_3_out, now0);
  and and_2 (and_2_out, In1, not_4_out, not_5_out, now1, not_6_out);
  and and_3 (and_3_out, not_7_out, not_8_out, not_9_out, now0);
  and and_4 (and_4_out, not_10_out, not_11_out, now1, not_12_out);
  and and_5 (and_5_out, not_13_out, not_14_out, not_15_out, not_16_out, now0);
  and and_6 (and_6_out, not_17_out, not_18_out, not_19_out, now1, not_20_out);
  and and_7 (and_7_out, not_21_out, In0, not_22_out, not_23_out);
  and and_8 (and_8_out, not_24_out, In0, not_25_out, now1, now0);
  or or_1 (out2, and_1_out, and_2_out);
  or or_2 (out1, and_3_out, and_4_out);
  or or_3 (out0, and_5_out, and_6_out, and_7_out, and_8_out);
endmodule
