// Logisim project ftoi.circ as structural Verilog: 1 circuit, main circuit ftoi
module ftoi (
  input  [15:0] in_1,
  output [31:0] out_2
);

  wire and_1_out, comparator_1_eq, comparator_2_eq;
  wire [4:0] negator_1_out, temp;
  wire [31:0] bit_extender_1_out, frac, multiplexer_1_out, multiplexer_3_out, negator_2_out, out,
       shifter_1_out, shifter_2_out;

  assign bit_extender_1_out = {{22{1'b0}}, in_1[9:0]};  // Bit_Extender bit_extender_1
  assign frac = bit_extender_1_out | 32'h400;  // OR_Gate or_1, 32 bits wide
  // Probe on frac
  Negator #(.width(5)) negator_1 (.in(temp), .out(negator_1_out));
  Shifter #(.width(32)) shifter_1 (.in(frac), .\dist (temp), .out(shifter_1_out));
  Shifter #(.width(32), .shift("lr")) shifter_2 (.in(frac), .\dist (negator_1_out), .out(shifter_2_out));
  Subtractor #(.width(5)) subtractor_1 (.a(in_1[14:10]), .b(5'b01111), .out(temp));  // open: bin, bout
  Multiplexer #(.width(32)) multiplexer_1 (
    .in0(shifter_1_out), .in1(shifter_2_out), .out(multiplexer_1_out), .sel(temp[4]));  // open: en
  Negator #(.width(32)) negator_2 (.in(out), .out(negator_2_out));
  Multiplexer #(.width(32)) multiplexer_2 (.in0(out), .in1(negator_2_out), .out(out_2), .sel(in_1[15]));  // open: en
  Comparator #(.width(5), .mode("unsigned")) comparator_1 (
    .a(in_1[14:10]), .b({5{1'b1}}), .eq(comparator_1_eq));  // open: gt, lt
  Comparator #(.width(5), .mode("unsigned")) comparator_2 (
    .a(in_1[14:10]), .b({5{1'b0}}), .eq(comparator_2_eq));  // open: gt, lt
  Multiplexer #(.width(32)) multiplexer_3 (
    .in0(multiplexer_1_out), .in1({32{1'b0}}), .out(multiplexer_3_out), .sel(and_1_out));  // open: en
  and and_1 (and_1_out, comparator_1_eq, comparator_2_eq);
  Shifter #(.width(32), .shift("lr")) shifter_3 (.in(multiplexer_3_out), .\dist (5'b01010), .out(out));

  // Other names for the same wires on the sheet: In[15:0] = in_1; M[4:0] = in_1[14:10]; sign = in_1[15]
endmodule
