// Logisim project grf.circ as structural Verilog: 1 circuit, main circuit grf
module grf (
  input  in_1,
  input  in_2,
  input  in_3,
  input  [4:0] A1,
  input  [4:0] A2,
  input  [4:0] A3,
  input  [31:0] wd,
  output [31:0] rd1,
  output [31:0] rd1_2
);

  wire [31:0] _0, _1, _2, _3, _4, _5, _6, _7, _8, _9, _10, _11, _12, _13, _14, _15, _16, _17, _18, _19, _20,
       _21, _22, _23, _24, _25, _26, _27, _28, _29, _30, _31, I0, I1, I2, I3, I4, I5, I6, I7, I8, I9, I10,
       I11, I12, I13, I14, I15, I16, I17, I18, I19, I20, I21, I22, I23, I24, I25, I26, I27, I28, I29, I30,
       I31;

  Multiplexer #(.select(5), .width(32)) multiplexer_1 (
    .in0(_0), .in1(_1), .in2(_2), .in3(_3), .in4(_4), .in5(_5), .in6(_6), .in7(_7), .in8(_8), .in9(_9),
    .in10(_10), .in11(_11), .in12(_12), .in13(_13), .in14(_14), .in15(_15), .in16(_16), .in17(_17),
    .in18(_18), .in19(_19), .in20(_20), .in21(_21), .in22(_22), .in23(_23), .in24(_24), .in25(_25),
    .in26(_26), .in27(_27), .in28(_28), .in29(_29), .in30(_30), .in31(_31), .out(rd1), .sel(A1));  // open: en
  Demultiplexer #(.select(5), .width(32), .tristate("true")) demultiplexer_1 (
    .out0(I0), .out1(I1), .out2(I2), .out3(I3), .out4(I4), .out5(I5), .out6(I6), .out7(I7), .out8(I8),
    .out9(I9), .out10(I10), .out11(I11), .out12(I12), .out13(I13), .out14(I14), .out15(I15), .out16(I16),
    .out17(I17), .out18(I18), .out19(I19), .out20(I20), .out21(I21), .out22(I22), .out23(I23), .out24(I24),
    .out25(I25), .out26(I26), .out27(I27), .out28(I28), .out29(I29), .out30(I30), .out31(I31), .in(wd),
    .sel(A3), .en(in_3));
  Multiplexer #(.select(5), .width(32)) multiplexer_2 (
    .in0(_0), .in1(_1), .in2(_2), .in3(_3), .in4(_4), .in5(_5), .in6(_6), .in7(_7), .in8(_8), .in9(_9),
    .in10(_10), .in11(_11), .in12(_12), .in13(_13), .in14(_14), .in15(_15), .in16(_16), .in17(_17),
    .in18(_18), .in19(_19), .in20(_20), .in21(_21), .in22(_22), .in23(_23), .in24(_24), .in25(_25),
    .in26(_26), .in27(_27), .in28(_28), .in29(_29), .in30(_30), .in31(_31), .out(rd1_2), .sel(A2));  // open: en
  // Probe on I1
  Register #(.width(32)) register_1 (.D(I0), .en(in_3), .Q(_0), .clk(in_1), .clr(1'b1));
  Register #(.width(32)) register_2 (.D(I6), .en(in_3), .Q(_6), .clk(in_1), .clr(in_2));
  Register #(.width(32)) register_3 (.D(I12), .en(in_3), .Q(_12), .clk(in_1), .clr(in_2));
  Register #(.width(32)) register_4 (.D(I18), .en(in_3), .Q(_18), .clk(in_1), .clr(in_2));
  Register #(.width(32)) register_5 (.D(I24), .en(in_3), .Q(_24), .clk(in_1), .clr(in_2));
  Register #(.width(32)) register_6 (.D(I30), .en(in_3), .Q(_30), .clk(in_1), .clr(in_2));
  // Probe on _1
  Register #(.width(32)) register_7 (.D(I1), .en(in_3), .Q(_1), .clk(in_1), .clr(in_2));
  Register #(.width(32)) register_8 (.D(I7), .en(in_3), .Q(_7), .clk(in_1), .clr(in_2));
  Register #(.width(32)) register_9 (.D(I13), .en(in_3), .Q(_13), .clk(in_1), .clr(in_2));
  Register #(.width(32)) register_10 (.D(I19), .en(in_3), .Q(_19), .clk(in_1), .clr(in_2));
  Register #(.width(32)) register_11 (.D(I25), .en(in_3), .Q(_25), .clk(in_1), .clr(in_2));
  Register #(.width(32)) register_12 (.D(I31), .en(in_3), .Q(_31), .clk(in_1), .clr(in_2));
  Register #(.width(32)) register_13 (.D(I2), .en(in_3), .Q(_2), .clk(in_1), .clr(in_2));
  Register #(.width(32)) register_14 (.D(I8), .en(in_3), .Q(_8), .clk(in_1), .clr(in_2));
  Register #(.width(32)) register_15 (.D(I14), .en(in_3), .Q(_14), .clk(in_1), .clr(in_2));
  Register #(.width(32)) register_16 (.D(I20), .en(in_3), .Q(_20), .clk(in_1), .clr(in_2));
  Register #(.width(32)) register_17 (.D(I26), .en(in_3), .Q(_26), .clk(in_1), .clr(in_2));
  Register #(.width(32)) register_18 (.D(I3), .en(in_3), .Q(_3), .clk(in_1), .clr(in_2));
  Register #(.width(32)) register_19 (.D(I9), .en(in_3), .Q(_9), .clk(in_1), .clr(in_2));
  Register #(.width(32)) register_20 (.D(I15), .en(in_3), .Q(_15), .clk(in_1), .clr(in_2));
  Register #(.width(32)) register_21 (.D(I21), .en(in_3), .Q(_21), .clk(in_1), .clr(in_2));
  Register #(.width(32)) register_22 (.D(I27), .en(in_3), .Q(_27), .clk(in_1), .clr(in_2));
  Register #(.width(32)) register_23 (.D(I4), .en(in_3), .Q(_4), .clk(in_1), .clr(in_2));
  Register #(.width(32)) register_24 (.D(I10), .en(in_3), .Q(_10), .clk(in_1), .clr(in_2));
  Register #(.width(32)) register_25 (.D(I16), .en(in_3), .Q(_16), .clk(in_1), .clr(in_2));
  Register #(.width(32)) register_26 (.D(I22), .en(in_3), .Q(_22), .clk(in_1), .clr(in_2));
  Register #(.width(32)) register_27 (.D(I28), .en(in_3), .Q(_28), .clk(in_1), .clr(in_2));
  Register #(.width(32)) register_28 (.D(I5), .en(in_3), .Q(_5), .clk(in_1), .clr(in_2));
  Register #(.width(32)) register_29 (.D(I11), .en(in_3), .Q(_11), .clk(in_1), .clr(in_2));
  Register #(.width(32)) register_30 (.D(I17), .en(in_3), .Q(_17), .clk(in_1), .clr(in_2));
  Register #(.width(32)) register_31 (.D(I23), .en(in_3), .Q(_23), .clk(in_1), .clr(in_2));
  Register #(.width(32)) register_32 (.D(I29), .en(in_3), .Q(_29), .clk(in_1), .clr(in_2));

  // Other names for the same wires on the sheet: clk = in_1; rd2[31:0] = rd1_2; reset = in_2; we = in_3
endmodule
