// Logisim project mod5.circ as structural Verilog: 1 circuit, main circuit mod5
module mod5 (
  input  In,
  output S0,
  output S1,
  output S2,
  output S3,
  output S4
);

  wire clock_1_out, decoder_1_out0, decoder_1_out1, decoder_1_out2, decoder_1_out3;
  wire [1:0] OUTPUT, register_1_q;

  Clock clock_1 (.out(clock_1_out));
  // Probe on register_1_q
  Register #(.width(2)) register_1 (.D(OUTPUT), .Q(register_1_q), .clk(clock_1_out));  // open: en, clr
  Decoder #(.select(2)) decoder_1 (
    .out0(decoder_1_out0), .out1(decoder_1_out1), .out2(decoder_1_out2), .out3(decoder_1_out3),
    .sel(register_1_q));  // open: en
  Multiplexer #(.width(2)) multiplexer_1 (.in0(2'b00), .in1(2'b01), .out(OUTPUT), .sel(In), .en(decoder_1_out0));
  Multiplexer #(.width(2)) multiplexer_2 (.in0(2'b11), .in1(2'b10), .out(OUTPUT), .sel(In), .en(decoder_1_out1));
  Multiplexer #(.width(2)) multiplexer_3 (.in0(2'b11), .in1(2'b10), .out(OUTPUT), .sel(In), .en(decoder_1_out2));
  Multiplexer #(.width(2)) multiplexer_4 (.in0(2'b00), .in1(2'b01), .out(OUTPUT), .sel(In), .en(decoder_1_out3));
  // Probe on OUTPUT
  Decoder #(.select(2)) decoder_2 (.out0(S1), .out1(S2), .out2(S3), .out3(S4), .sel(OUTPUT));  // open: en

  assign S0 = 1'b0;
endmodule
