// Logisim project navigation.circ as structural Verilog: 3 circuits, main circuit navigation
module navigation (
  input  [1:0] in_1,
  input  in_2,
  input  in_3,
  output arrive,
  output hit
);

  wire comparator_1_eq;
  wire [2:0] next_state_1_out0, now;

  Clock clock_1 ();  // open: out
  next_state next_state_1 (
    .n2(now[2]), .n1(now[1]), .n0(now[0]), .out2(next_state_1_out0[2]), .In1(in_1[1]), .In0(in_1[0]),
    .out1(next_state_1_out0[1]), .out0(next_state_1_out0[0]));
  // Probe on next_state_1_out0
  Register #(.width(3)) register_1 (.D(next_state_1_out0), .Q(now), .clk(in_2), .clr(in_3));  // open: en
  print print_1 (.now(now), .out_2(arrive));
  Comparator #(.width(3), .mode("unsigned")) comparator_1 (
    .a(next_state_1_out0), .b(now), .eq(comparator_1_eq));  // open: gt, lt
  // Probe on now
  Register #(.width(1)) register_2 (.D(comparator_1_eq), .Q(hit), .clk(in_2), .clr(in_3));  // open: en

  // Other names for the same wires on the sheet: clk = in_2; dir[1:0] = in_1; reset = in_3
endmodule

module next_state (
  input  n2,
  input  n1,
  input  n0,
  input  In1,
  input  In0,
  output out2,
  output out1,
  output out0
);

  wire and_1_out, and_2_out, and_3_out, and_4_out, and_5_out, and_6_out, and_7_out, and_8_out, and_9_out,
       and_10_out, and_11_out, not_1_out, not_2_out, not_3_out, not_4_out, not_5_out, not_6_out, not_7_out,
       not_8_out, not_9_out, not_10_out, not_11_out, not_12_out, not_13_out, not_14_out, not_15_out,
       not_16_out, not_17_out, not_18_out, not_19_out, not_20_out, not_21_out, not_22_out, not_23_out,
       not_24_out;

  not not_1 (not_1_out, n2);
  not not_2 (not_2_out, n1);
  not not_3 (not_3_out, In1);
  not not_4 (not_4_out, In0);
  not not_5 (not_5_out, n0);
  not not_6 (not_6_out, In1);
  not not_7 (not_7_out, In0);
  not not_8 (not_8_out, n0);
  not not_9 (not_9_out, n2);
  not not_10 (not_10_out, In1);
  not not_11 (not_11_out, n2);
  not not_12 (not_12_out, In0);
  not not_13 (not_13_out, n0);
  not not_14 (not_14_out, In1);
  not not_15 (not_15_out, n0);
  not not_16 (not_16_out, n2);
  not not_17 (not_17_out, n1);
  not not_18 (not_18_out, n0);
  not not_19 (not_19_out, In1);
  not not_20 (not_20_out, In0);
  not not_21 (not_21_out, n2);
  not not_22 (not_22_out, n2);
  not not_23 (not_23_out, n0);
  not not_24 (not_24_out, In0);
  and and_1 (and_1_out, not_1_out, not_2_out, n0, not_3_out, not_4_out);
  and and_2 (and_2_out, n2, n1, not_5_out, not_6_out, not_7_out);
  and and_3 (and_3_out, n2, n1, not_8_out, In1, In0);
  and and_4 (and_4_out, not_9_out, n0, not_10_out);
  and and_5 (and_5_out, not_11_out, n1, n0, not_12_out);
  and and_6 (and_6_out, n2, n1, not_13_out, not_14_out);
  and and_7 (and_7_out, n2, n1, not_15_out, In0);
  and and_8 (and_8_out, not_16_out, not_17_out, not_18_out, not_19_out, not_20_out);
  and and_9 (and_9_out, not_21_out, n0, In0);
  and and_10 (and_10_out, not_22_out, n1, n0, In1);
  and and_11 (and_11_out, n2, n1, not_23_out, In1, not_24_out);
  or or_1 (out2, and_1_out, and_2_out, and_3_out);
  or or_2 (out1, and_4_out, and_5_out, and_6_out, and_7_out);
  or or_3 (out0, and_8_out, and_9_out, and_10_out, and_11_out);
endmodule

module print (
  input  [2:0] now,
  output out_2
);

  Comparator #(.width(3), .mode("unsigned")) comparator_1 (.a(now), .b(3'b010), .eq(out_2));  // open: gt, lt
endmodule
