// Logisim project swap.circ as structural Verilog: 1 circuit, main circuit swap
module swap (
  input  I1,
  input  I2,
  input  S,
  output O1,
  output O2
);

  wire and_1_out, and_2_out, and_3_out, and_4_out, and_5_out, and_6_out, and_7_out, and_8_out, not_1_out,
       not_2_out, not_3_out, not_4_out, not_5_out, not_6_out, not_7_out, not_8_out;

  not not_1 (not_1_out, S);
  not not_2 (not_2_out, S);
  not not_3 (not_3_out, I2);
  not not_4 (not_4_out, I1);
  not not_5 (not_5_out, S);
  not not_6 (not_6_out, S);
  not not_7 (not_7_out, I1);
  not not_8 (not_8_out, I2);
  and and_1 (and_1_out, not_1_out, I2, I1);
  and and_2 (and_2_out, not_2_out, I1, not_3_out);
  and and_3 (and_3_out, not_4_out, S, I2);
  and and_4 (and_4_out, I1, I2, S);
  and and_5 (and_5_out, not_5_out, I2, I1);
  and and_6 (and_6_out, I1, I2, S);
  and and_7 (and_7_out, not_6_out, not_7_out, I2);
  and and_8 (and_8_out, S, I1, not_8_out);
  or or_1 (O1, and_1_out, and_2_out, and_3_out, and_4_out);
  or or_2 (O2, and_5_out, and_6_out, and_7_out, and_8_out);
endmodule
